# Fritzing sketch Circuit_Diagram (saved by Fritzing 0.9.3b)

parts:
  S1 = Pushbutton [package="[THT]"]
  S2 = Pushbutton [package="[THT]"]
  Driver1 = 28BYJ-48 Driver Module [part_number=ULN2003 package=THT]
  SM1 = 28BYJ-48 Stepper Motor [part_number=28BYJ-48]  # not connected
  TP1 = TP4056 [chip_label=TP4056 package="DIP (Dual Inline) [THT]"]
  A1 = Esp32-c3 super mini
  U1 = LIPO-2000mAh [package=lipo-2000]
  U2 = Mini-360 DC-DC Buck converter [package=THT]
  A2 = Solar charger SD05CRMA
  D1 = SOLAR-IXYS [package=solarbit-12x1]

nets:
  N1: S1.Pin_1, S1.Pin_2, S2.Pin_3, S2.Pin_4, Driver1.GND, A1.Pin_15, U2.OUT-
  N2: S1.Pin_3, A1.Pin_7
  N3: S2.Pin_1, A1.Pin_8
  N4: Driver1.IN1, A1.Pin_12
  N5: Driver1.IN2, A1.Pin_11
  N6: Driver1.IN3, A1.Pin_10
  N7: Driver1.IN4, A1.Pin_9
  N8: Driver1.Vmotor, A1.Pin_16, U2.OUT+
  N9: TP1.pin3, U2.IN+
  N10: TP1.pin4, U1.+, A2.Pin_4
  N11: TP1.pin5, U1.-, A2.Pin_2, A2.Pin_3, D1.A
  N12: TP1.pin6, U2.IN-
  N13: A2.Pin_1, D1.C

custom parts:
  28BYJ-48 Driver Module: Generic male header
  28BYJ-48 Stepper Motor: Unipolar Stepper Motor 28BYJ-48 Top coil - pink & orange Bottom coil - blue & yellow Common rail - red Connector pins: blue - pink - yellow - orange - red
  TP4056: A DIP stand-in part for whatever IC you want. With 6 pins on a 300mil dual inline package (DIP) footprint.
  Esp32-c3 super mini: ESP32-C3 Development Board ESP32 SuperMini Development Board ESP32 Development Board WiFi Bluetooth.
  Mini-360 DC-DC Buck converter: Mini-360 DC-DC Buck converter. Tiny buck step down voltage converter, input voltage 4.75 to 23V output 1 to 17V adjustable. Available from ebay and the like.
  Solar charger SD05CRMA: SD05CRMA 4.4-6.5V Input Solar Panel Dedicated Charging Module 18650 LiPo Li-ion Lithium Battery Charge Controller Module.
